# Fritzing sketch Shaking_incubator_Elexctric_Wiring  (saved by Fritzing 0.9.3b)
perfboards: 3

parts:
  Display1 = LCD screen 16x2 IIC [part_number=101290]
  Matrix_keypad1 = KEYPAD 4x4
  Composant4 = Arduino Uno (Rev3)
  U1 = POT [package=pot_alpha_rv16af-20]
  R1 = Resistor [tolerance=±5% resistance=220 package="0805 [SMD]"]
  2_Channel_Relay1 = 2 Channel Power Relay
  Composant5 = Arduino Nano (Rev3.0)
  LED1 = smd LED [color="Green (555nm)" package="0603 [SMD]"]  # not connected
  LED2 = smd LED [color="Green (555nm)" package="0603 [SMD]"]  # not connected
  LED3 = smd LED [color="Green (555nm)" package="0603 [SMD]"]  # not connected
  LED4 = smd LED [color="Green (555nm)" package="0603 [SMD]"]  # not connected
  LED5 = smd LED [color="Green (555nm)" package="0603 [SMD]"]  # not connected
  R3 = Resistor [tolerance=±5% resistance=220 package="0805 [SMD]"]  # not connected
  R4 = Resistor [tolerance=±5% resistance=220 package="0805 [SMD]"]  # not connected
  R5 = Resistor [tolerance=±5% resistance=220 package="0805 [SMD]"]  # not connected
  R6 = Resistor [tolerance=±5% resistance=220 package="0805 [SMD]"]
  R7 = Resistor [tolerance=±5% resistance=220 package="0805 [SMD]"]  # not connected
  Pololu_A1 = Pololu A4988 [package=SO16]
  M2 = Stepper Motor - Bipolar
  J1 = Power Jack [package=power_jack_smd]
  R8 = Resistor [tolerance=±5% resistance=220 package="0805 [SMD]"]
  DS2 = DS18B20 1-Wire Temperature Sensor Probe Cable
  Ventilateur = DC Motor

nets:
  N1: Display1.SDA, Composant4.A4/SDA
  N2: Display1.SCL, Composant4.A5/SCL
  N3: Matrix_keypad1.col1, Composant4.D9_PWM
  N4: Matrix_keypad1.col2, Composant4.D8
  N5: Matrix_keypad1.col3, Composant4.D7
  N6: Matrix_keypad1.col4, Composant4.D6_PWM
  N7: Matrix_keypad1.row1, Composant4.D5_PWM
  N8: Matrix_keypad1.row2, Composant4.D4
  N9: Matrix_keypad1.row3, Composant4.D3_PWM
  N10: Matrix_keypad1.row4, Composant4.D2
  N11: Composant4.A0, U1.A, R1.Pin_1, Composant5.A0
  N12: Composant4.D10_PWM/SS, R8.Pin_0, DS2.DQ
  N13: Composant4.D11_PWM/MOSI, 2_Channel_Relay1.IN1
  N14: Composant4.D12/MISO, 2_Channel_Relay1.IN2
  N15: Composant4.D0/RX, Composant5.D1/TX
  N16: Composant4.D1/TX, Composant5.D0/RX
  VIN: Composant4.VIN, 2_Channel_Relay1.K2-COM, Composant5.VIN, J1.GNDBREAK
  5V: U1.S, Composant5.5V, R8.Pin_1, DS2.VDD
  GND: R1.Pin_0, 2_Channel_Relay1.GND, Composant5.GND, J1.GND, DS2.GND, Ventilateur.pin_2
  N17: 2_Channel_Relay1.JD-VCC, 2_Channel_Relay1.VCC#9
  N18: 2_Channel_Relay1.K2-NC, Ventilateur.pin_1
  N19: Composant5.D9, R6.Pin_0
  N20: Composant5.D11/MOSI, Pololu_A1.STEP
  N21: Composant5.D12/MISO, Pololu_A1.DIR
  N22: Pololu_A1.RESET, Pololu_A1.SLEEP
  N23: Pololu_A1.1B, M2.D
  N24: Pololu_A1.1A, M2.B
  N25: Pololu_A1.2A, M2.C
  N26: Pololu_A1.2B, M2.A

custom parts:
  LCD screen 16x2 IIC: LCD screen with HD44780 controller enables showing text, symbols, value or anything else that comes from Croduino/Arduino. It is capable of showing 16 symbols in two lines and therefore can be used in many projects that need to send clearly visible and legible output information.. • Color of symbols: White • Backlight: Blue • Dimensions: 80 x 36 x 12 mm • Screen dimensions: 64.5 x 16 mm •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
  KEYPAD 4x4: Matrix keypad 16 buttons, 4 rows x 4 columns
  2 Channel Power Relay: A 2 channel power relay. The module operates at 5V.
